// Logisim project p6.circ as structural Verilog: 11 circuits, main circuit main
module main (
);

  wire d_cmp_1_jump, D_Fwd_rs_data, d_grf_1_rd1, d_grf_1_rd2, d_npc_1_npc, D_rs_addr, D_rt_addr, e_alu_1_c,
       E_ALUASel, E_ALUBSel, E_Fwd_rs_data, E_Fwd_rt_data, E_GRFWD, e_mdu_1_hi, e_mdu_1_lo, E_PC_8,
       f_im_1_instr, f_pc_1_pc, imm16, imm32, m_dm_1_rd, M_Fwd_rt_data, M_GRFWD, M_PC_8, multiplexer_1_out,
       multiplexer_2_out, multiplexer_5_out, multiplexer_6_out, multiplexer_8_out, not_1_out, Stall,
       undriven, W_GRFA3, W_GRFWD, W_PC_8;
  wire [1:0] E_ALUOutSel, E_GRFWDSel, M_GRFWDSel, W_GRFWDSel;

  F_PC f_pc_1 (.NPC(d_npc_1_npc), .PC(f_pc_1_pc));  // open: WE
  F_IM f_im_1 (.PC(f_pc_1_pc), .Instr(f_im_1_instr));
  not not_1 (not_1_out, Stall);
  \reg  reg_1 (.WE(not_1_out));  // open: flush
  D_NPC d_npc_1 (
    .D_PC(f_pc_1_pc), .F_PC(f_pc_1_pc), .Addr(D_Fwd_rs_data), .NPC(d_npc_1_npc));  // open: imm16, imm26, jump
  D_GRF d_grf_1 (.A1(D_rs_addr), .RD1(d_grf_1_rd1), .A2(D_rt_addr), .RD2(d_grf_1_rd2));  // open: A3, WD
  D_CMP d_cmp_1 (.rs_data(multiplexer_1_out), .rt_data(multiplexer_2_out), .jump(d_cmp_1_jump));
  Multiplexer #(.select(2)) multiplexer_1 (
    .in0(d_grf_1_rd1), .in1(M_GRFWD), .in2(E_GRFWD), .out(multiplexer_1_out));  // open: in3, sel, en
  Multiplexer #(.select(2)) multiplexer_2 (
    .in0(d_grf_1_rd2), .in1(M_GRFWD), .in2(E_GRFWD), .out(multiplexer_2_out));  // open: in3, sel, en
  D_EXT d_ext_1 (.imm16(imm16), .imm32(imm32));
  \reg  reg_2 (.flush(Stall));  // open: WE
  Multiplexer #(.select(2)) multiplexer_3 (
    .in0(multiplexer_1_out), .in1(W_GRFWD), .in2(M_GRFWD), .out(E_Fwd_rs_data));  // open: in3, sel, en
  Multiplexer #(.select(2)) multiplexer_4 (
    .in0(multiplexer_2_out), .in1(W_GRFWD), .in2(M_GRFWD), .out(E_Fwd_rt_data));  // open: in3, sel, en
  Multiplexer multiplexer_5 (
    .in0(E_Fwd_rs_data), .in1(undriven), .out(multiplexer_5_out), .sel(E_ALUASel));  // open: en
  Multiplexer multiplexer_6 (.in0(E_Fwd_rt_data), .in1(imm32), .out(multiplexer_6_out), .sel(E_ALUBSel));  // open: en
  Multiplexer #(.select(2)) multiplexer_7 (.in2(E_PC_8), .out(E_GRFWD), .sel(E_GRFWDSel));  // open: in0, in1, in3, en
  E_ALU e_alu_1 (.A(multiplexer_5_out), .B(multiplexer_6_out), .C(e_alu_1_c));
  E_MDU e_mdu_1 (.D1(E_Fwd_rs_data), .D2(E_Fwd_rt_data), .HI(e_mdu_1_hi), .LO(e_mdu_1_lo));
  \reg  reg_3 ();  // open: WE, flush
  Multiplexer #(.select(2)) multiplexer_8 (
    .in0(e_alu_1_c), .in1(e_mdu_1_hi), .in2(e_mdu_1_lo), .out(multiplexer_8_out), .sel(E_ALUOutSel));  // open: in3, en
  Multiplexer multiplexer_9 (.in0(E_Fwd_rt_data), .in1(W_GRFWD), .out(M_Fwd_rt_data));  // open: sel, en
  Multiplexer #(.select(2)) multiplexer_10 (
    .in0(multiplexer_8_out), .in2(M_PC_8), .out(M_GRFWD), .sel(M_GRFWDSel));  // open: in1, in3, en
  \reg  reg_4 ();  // open: WE, flush
  M_DM m_dm_1 (.A(multiplexer_8_out), .WD(M_Fwd_rt_data), .RD(m_dm_1_rd));
  Multiplexer #(.select(2)) multiplexer_11 (
    .in0(multiplexer_8_out), .in1(m_dm_1_rd), .in2(W_PC_8), .out(W_GRFWD), .sel(W_GRFWDSel));  // open: in3, en
  D_GRF d_grf_2 (.A3(W_GRFA3), .WD(W_GRFWD));  // open: A1, RD1, A2, RD2

  // Notes on the sheet:
  //   PC
  //   F_Instr
  //   F/D
  //   F_PC
  //   NPC
  //   D_Instr
  //   D_PC
  //   F_PC
  //   D_rs_data
  //   D_rt_data
  //   D_Fwd_rs_data
  //   D_Fwd_rt_data
  //   D_jump
  //   D/E
  //   D_imm32
  //   E_jump
  //   E_rs_data
  //   E_rt_data
  //   shamt
  //   E_imm32
  //   E_ALUC
  //   E/M
  //   M_jump
  //   M_rt_data
  //   M_ALUOut
  //   M_DmRD
  //   W_jump
  //   M/W
  //   W_DmRD
  //   W_ALUOut
endmodule

module F_PC (
  input  NPC,
  input  WE,
  output PC
);
endmodule

module F_IM (
  input  PC,
  output Instr
);
endmodule

module D_GRF (
  input  A1,
  input  A2,
  input  A3,
  input  WD,
  output RD1,
  output RD2
);
endmodule

module D_EXT (
  input  imm16,
  output imm32
);
endmodule

module D_NPC (
  input  D_PC,
  input  F_PC,
  input  imm16,
  input  imm26,
  input  Addr,
  input  jump,
  output NPC
);
endmodule

module D_CMP (
  input  rs_data,
  input  rt_data,
  output jump
);
endmodule

module E_ALU (
  input  A,
  input  B,
  output C
);
endmodule

module M_DM (
  input  WD,
  input  A,
  output RD
);
endmodule

module \reg  (
  input  WE,
  input  flush
);
endmodule

module E_MDU (
  input  D1,
  input  D2,
  output HI,
  output LO
);
endmodule
