// Logisim project CRC_8bit.circ as structural Verilog: 2 circuits, main circuit CRC
module CRC (
  input  [7:0] A,
  input  [3:0] B,
  output [10:0] C
);

  wire _0, _1, _2, _3, _4, _5, _6;
  wire [2:0] CRC, \n4bit模二除法器_1_余数 , \n4bit模二除法器_2_余数 , \n4bit模二除法器_3_余数 , \n4bit模二除法器_4_余数 ,
       \n4bit模二除法器_5_余数 , \n4bit模二除法器_6_余数 ;
  wire [3:1] \n4bit模二除法器_7_余数 ;
  wire [10:0] bit_extender_1_out, bit_extender_2_out;
  wire [10:7] \被除数 ;

  // Probe on CRC
  assign bit_extender_1_out = {{8{1'b0}}, CRC};  // Bit_Extender bit_extender_1
  // Probe on bit_extender_2_out
  assign bit_extender_2_out = {{3{1'b0}}, A};  // Bit_Extender bit_extender_2
  assign C = {\被除数 , _6, _5, _4, _3, _2, _1, _0} | bit_extender_1_out;  // OR_Gate or_1, 11 bits wide
  // Probe on {\被除数 , _6, _5, _4, _3, _2, _1, _0}
  Shifter #(.width(11)) shifter_1 (
    .in(bit_extender_2_out), .\dist (4'b0011), .out({\被除数 , _6, _5, _4, _3, _2, _1, _0}));
  \_4bit模二除法器  \u_4bit模二除法器_1  (.\被除数 (\被除数 ), .\除数 (B), .\余数 (\n4bit模二除法器_1_余数 ));  // open: 商
  // Probe on \n4bit模二除法器_1_余数 
  // Probe on {\n4bit模二除法器_1_余数 , _6}
  // Probe on {\n4bit模二除法器_2_余数 , _5}
  \_4bit模二除法器  \u_4bit模二除法器_2  (.\被除数 ({\n4bit模二除法器_1_余数 , _6}), .\除数 (B), .\余数 (\n4bit模二除法器_2_余数 ));  // open: 商
  // Probe on \n4bit模二除法器_2_余数 
  \_4bit模二除法器  \u_4bit模二除法器_3  (.\被除数 ({\n4bit模二除法器_2_余数 , _5}), .\除数 (B), .\余数 (\n4bit模二除法器_3_余数 ));  // open: 商
  // Probe on \n4bit模二除法器_3_余数 
  // Probe on {\n4bit模二除法器_3_余数 , _4}
  \_4bit模二除法器  \u_4bit模二除法器_4  (.\被除数 ({\n4bit模二除法器_3_余数 , _4}), .\除数 (B), .\余数 (\n4bit模二除法器_4_余数 ));  // open: 商
  // Probe on \n4bit模二除法器_4_余数 
  // Probe on {\n4bit模二除法器_4_余数 , _3}
  // Probe on {\n4bit模二除法器_5_余数 , _2}
  \_4bit模二除法器  \u_4bit模二除法器_5  (.\被除数 ({\n4bit模二除法器_4_余数 , _3}), .\除数 (B), .\余数 (\n4bit模二除法器_5_余数 ));  // open: 商
  // Probe on \n4bit模二除法器_5_余数 
  \_4bit模二除法器  \u_4bit模二除法器_6  (.\被除数 ({\n4bit模二除法器_5_余数 , _2}), .\除数 (B), .\余数 (\n4bit模二除法器_6_余数 ));  // open: 商
  // Probe on \n4bit模二除法器_6_余数 
  // Probe on {\n4bit模二除法器_6_余数 , _1}
  \_4bit模二除法器  \u_4bit模二除法器_7  (.\被除数 ({\n4bit模二除法器_6_余数 , _1}), .\除数 (B), .\余数 (\n4bit模二除法器_7_余数 ));  // open: 商
  // Probe on {\n4bit模二除法器_7_余数 , _0}
  // Probe on \n4bit模二除法器_7_余数 
  \_4bit模二除法器  \u_4bit模二除法器_8  (.\被除数 ({\n4bit模二除法器_7_余数 , _0}), .\除数 (B), .\余数 (CRC));  // open: 商

  // Other names for the same wires on the sheet: 被除数[6:0] = {_6, _5, _4, _3, _2, _1, _0}; 除数[3:0] = B
endmodule

module \_4bit模二除法器  (
  input  [3:0] \被除数 ,
  input  [3:0] \除数 ,
  output [2:0] \余数 ,
  output \商 
);

  wire [3:0] multiplexer_1_out, xor_1_out;

  BitSelector #(.width(4)) bitselector_1 (.in(\被除数 ), .out(\商 ), .sel(2'b11));
  assign xor_1_out = \被除数  ^ \除数 ;  // XOR_Gate xor_1, 4 bits wide
  // Probe on multiplexer_1_out
  Bit_Extender #(.in_width(4), .out_width(3)) bit_extender_1 (.in(multiplexer_1_out), .out(\余数 ));
  Multiplexer #(.width(4)) multiplexer_1 (
    .in0(\被除数 ), .in1(xor_1_out), .out(multiplexer_1_out), .sel(\商 ));  // open: en

  // Other names for the same wires on the sheet: A[3:0] = \被除数 ; B[3:0] = \除数 ; C[2:0] = \余数 ; 最高位 = \商 
endmodule
