// Logisim project FSM.circ as structural Verilog: 2 circuits, main circuit fsm
module fsm (
  input  CLR,
  input  [1:0] In,
  output Z
);

  wire clk, comparator_1_eq, comparator_2_eq;
  wire [2:0] multiplexer_1_out, now, pre;

  Clock clock_1 (.out(clk));
  // Probe on pre
  // Probe on now
  \状态转移  \u_状态转移_1  (
    .pre2(pre[2]), .pre1(pre[1]), .pre0(pre[0]), .in1(In[1]), .in0(In[0]), .now2(now[2]), .now1(now[1]),
    .now0(now[0]));
  Comparator #(.width(3), .mode("unsigned")) comparator_1 (.a(now), .b(3'b011), .eq(comparator_1_eq));  // open: gt, lt
  Comparator #(.width(3), .mode("unsigned")) comparator_2 (.a(now), .b(3'b110), .eq(comparator_2_eq));  // open: gt, lt
  Multiplexer #(.width(3)) multiplexer_1 (.in0(now), .in1(3'b000), .out(multiplexer_1_out), .sel(CLR));  // open: en
  Register #(.width(3)) register_1 (.D(multiplexer_1_out), .Q(pre), .clk(clk));  // open: en, clr
  or or_1 (Z, comparator_1_eq, comparator_2_eq);
endmodule

module \状态转移  (
  input  pre2,
  input  pre1,
  input  pre0,
  input  in1,
  input  in0,
  output now2,
  output now1,
  output now0
);

  wire and_1_out, and_2_out, and_3_out, and_4_out, and_5_out, and_6_out, and_7_out, and_8_out, and_9_out,
       and_10_out, not_1_out, not_2_out, not_3_out, not_4_out, not_5_out, not_6_out, not_7_out, not_8_out,
       not_9_out, not_10_out, not_11_out, not_12_out, not_13_out, not_14_out, not_15_out, not_16_out,
       not_17_out, not_18_out, not_19_out, not_20_out, not_21_out, not_22_out, not_23_out, not_24_out;

  not not_1 (not_1_out, pre2);
  not not_2 (not_2_out, pre1);
  not not_3 (not_3_out, in1);
  not not_4 (not_4_out, pre1);
  not not_5 (not_5_out, pre0);
  not not_6 (not_6_out, in1);
  not not_7 (not_7_out, pre1);
  not not_8 (not_8_out, in0);
  not not_9 (not_9_out, pre1);
  not not_10 (not_10_out, in0);
  not not_11 (not_11_out, pre2);
  not not_12 (not_12_out, pre0);
  not not_13 (not_13_out, in0);
  not not_14 (not_14_out, pre2);
  not not_15 (not_15_out, pre0);
  not not_16 (not_16_out, in1);
  not not_17 (not_17_out, pre2);
  not not_18 (not_18_out, pre0);
  not not_19 (not_19_out, in0);
  not not_20 (not_20_out, in1);
  not not_21 (not_21_out, pre1);
  not not_22 (not_22_out, pre0);
  not not_23 (not_23_out, in0);
  not not_24 (not_24_out, in1);
  and and_1 (and_1_out, not_1_out, not_2_out, pre0, not_3_out, in0);
  and and_2 (and_2_out, pre2, not_4_out, not_5_out, not_6_out);
  and and_3 (and_3_out, pre2, not_7_out, not_8_out);
  and and_4 (and_4_out, not_9_out, pre0, not_10_out);
  and and_5 (and_5_out, not_11_out, pre1, not_12_out, not_13_out);
  and and_6 (and_6_out, not_14_out, not_15_out, not_16_out, in0);
  and and_7 (and_7_out, not_17_out, pre1, not_18_out, not_19_out);
  and and_8 (and_8_out, pre1, not_20_out, in0);
  and and_9 (and_9_out, pre2, not_21_out, not_22_out, not_23_out);
  and and_10 (and_10_out, pre2, pre0, not_24_out, in0);
  or or_1 (now2, and_1_out, and_2_out, and_3_out);
  or or_2 (now1, and_4_out, and_5_out);
  or or_3 (now0, and_6_out, and_7_out, and_8_out, and_9_out, and_10_out);
endmodule
