// Logisim project ftoi.circ as structural Verilog: 1 circuit, main circuit ftoi
module ftoi (
  input  [15:0] float,
  output [31:0] \int 
);

  wire comparator_1_eq, comparator_2_eq, or_1_out, subtractor_1_bout;
  wire [4:0] subtractor_1_out;
  wire [31:0] bit_extender_1_out, multiplexer_1_out, negator_1_out, shifter_1_out;

  Subtractor #(.width(5)) subtractor_1 (
    .a(float[14:10]), .b(5'b01111), .out(subtractor_1_out), .bout(subtractor_1_bout));  // open: bin
  Shifter #(.width(32)) shifter_1 (.in({22'h1, float[9:0]}), .\dist (subtractor_1_out), .out(shifter_1_out));
  Comparator #(.width(5), .mode("unsigned")) comparator_1 (
    .a(float[14:10]), .b({5{1'b1}}), .eq(comparator_1_eq));  // open: gt, lt
  Comparator #(.width(5), .mode("unsigned")) comparator_2 (
    .a(float[14:10]), .b({5{1'b0}}), .eq(comparator_2_eq));  // open: gt, lt
  assign bit_extender_1_out = {{10{1'b0}}, shifter_1_out[31:10]};  // Bit_Extender bit_extender_1
  Negator #(.width(32)) negator_1 (.in(bit_extender_1_out), .out(negator_1_out));
  Multiplexer #(.width(32)) multiplexer_1 (
    .in0(bit_extender_1_out), .in1(negator_1_out), .out(multiplexer_1_out), .sel(float[15]));  // open: en
  or or_1 (or_1_out, comparator_1_eq, subtractor_1_bout, comparator_2_eq);
  Multiplexer #(.width(32)) multiplexer_2 (
    .in0(multiplexer_1_out), .in1({32{1'b0}}), .out(\int ), .sel(or_1_out));  // open: en

  // Other names for the same wires on the sheet: in[15:0] = float; out[31:0] = \int 
endmodule
