// Logisim project navigation.circ as structural Verilog: 3 circuits, main circuit navigation
module navigation (
  input  [1:0] dir,
  input  clk,
  input  reset,
  output arrive,
  output hit
);

  wire \状态转移_1_hit ;
  wire [2:0] pre, \状态转移_1_now3 ;

  // Probe on pre
  \状态转移  \u_状态转移_1  (
    .pre1(pre[2]), .pre2(pre[1]), .pre3(pre[0]), .dir1(dir[1]), .dir2(dir[0]), .now1(\状态转移_1_now3 [2]),
    .now2(\状态转移_1_now3 [1]), .now3(\状态转移_1_now3 [0]), .hit(\状态转移_1_hit ));
  // Probe on dir
  // Probe on \状态转移_1_now3 
  Register #(.width(1)) register_1 (.D(\状态转移_1_hit ), .Q(hit), .clk(clk), .clr(reset));  // open: en
  Register #(.width(3)) \u_状态存储  (.D(\状态转移_1_now3 ), .Q(pre), .clk(clk), .clr(reset));  // open: en
  \状态输出  \u_状态输出_1  (.s1(pre[2]), .s2(pre[1]), .s3(pre[0]), .arrive(arrive));

  // Other names for the same wires on the sheet: rst = reset
endmodule

module \状态转移  (
  input  pre1,
  input  pre2,
  input  pre3,
  input  dir1,
  input  dir2,
  output now1,
  output now2,
  output now3,
  output hit
);

  wire and_1_out, and_2_out, and_3_out, and_4_out, and_5_out, and_6_out, and_7_out, and_8_out, and_9_out,
       and_10_out, and_11_out, and_12_out, and_13_out, and_14_out, and_15_out, and_16_out, not_1_out,
       not_2_out, not_3_out, not_4_out, not_5_out, not_6_out, not_7_out, not_8_out, not_9_out, not_10_out,
       not_11_out, not_12_out, not_13_out, not_14_out, not_15_out, not_16_out, not_17_out, not_18_out,
       not_19_out, not_20_out, not_21_out, not_22_out, not_23_out, not_24_out, not_25_out, not_26_out,
       not_27_out, not_28_out, not_29_out, not_30_out, not_31_out, not_32_out, not_33_out, not_34_out,
       not_35_out, not_36_out, not_37_out, not_38_out, not_39_out, not_40_out;

  not not_1 (not_1_out, pre1);
  not not_2 (not_2_out, pre3);
  not not_3 (not_3_out, dir1);
  not not_4 (not_4_out, dir2);
  not not_5 (not_5_out, pre1);
  not not_6 (not_6_out, dir1);
  not not_7 (not_7_out, pre1);
  not not_8 (not_8_out, pre2);
  not not_9 (not_9_out, dir1);
  not not_10 (not_10_out, pre1);
  not not_11 (not_11_out, dir1);
  not not_12 (not_12_out, dir2);
  not not_13 (not_13_out, pre1);
  not not_14 (not_14_out, pre3);
  not not_15 (not_15_out, dir1);
  not not_16 (not_16_out, pre1);
  not not_17 (not_17_out, pre3);
  not not_18 (not_18_out, dir2);
  not not_19 (not_19_out, pre1);
  not not_20 (not_20_out, pre1);
  not not_21 (not_21_out, pre2);
  not not_22 (not_22_out, dir1);
  not not_23 (not_23_out, dir2);
  not not_24 (not_24_out, pre1);
  not not_25 (not_25_out, pre1);
  not not_26 (not_26_out, pre1);
  not not_27 (not_27_out, dir2);
  not not_28 (not_28_out, pre1);
  not not_29 (not_29_out, pre3);
  not not_30 (not_30_out, dir1);
  not not_31 (not_31_out, pre1);
  not not_32 (not_32_out, pre2);
  not not_33 (not_33_out, pre3);
  not not_34 (not_34_out, pre1);
  not not_35 (not_35_out, pre3);
  not not_36 (not_36_out, dir2);
  not not_37 (not_37_out, pre1);
  not not_38 (not_38_out, pre1);
  not not_39 (not_39_out, dir1);
  not not_40 (not_40_out, dir2);
  and and_1 (and_1_out, not_1_out, pre2, not_2_out, not_3_out, not_4_out);
  and and_2 (and_2_out, not_5_out, pre2, pre3, not_6_out, dir2);
  and and_3 (and_3_out, not_7_out, not_8_out, pre3, not_9_out);
  and and_4 (and_4_out, not_10_out, pre3, not_11_out, not_12_out);
  and and_5 (and_5_out, not_13_out, pre2, not_14_out, not_15_out, dir2);
  and and_6 (and_6_out, not_16_out, pre2, not_17_out, dir1, not_18_out);
  and and_7 (and_7_out, not_19_out, pre2, pre3, dir1, dir2);
  and and_8 (and_8_out, not_20_out, not_21_out, not_22_out, not_23_out);
  and and_9 (and_9_out, not_24_out, pre3, dir1, dir2);
  and and_10 (and_10_out, not_25_out, pre2, dir1, dir2);
  and and_11 (and_11_out, not_26_out, pre2, pre3, not_27_out);
  and and_12 (and_12_out, not_28_out, not_29_out, not_30_out, dir2);
  and and_13 (and_13_out, not_31_out, not_32_out, not_33_out, dir1);
  and and_14 (and_14_out, not_34_out, not_35_out, dir1, not_36_out);
  and and_15 (and_15_out, not_37_out, pre3, dir1, dir2);
  and and_16 (and_16_out, not_38_out, pre2, pre3, not_39_out, not_40_out);
  or or_1 (now1, and_1_out, and_2_out);
  or or_2 (now2, and_3_out, and_4_out, and_5_out, and_6_out, and_7_out);
  or or_3 (now3, and_8_out, and_9_out, and_10_out, and_11_out);
  or or_4 (hit, and_12_out, and_13_out, and_14_out, and_15_out, and_16_out);
endmodule

module \状态输出  (
  input  s1,
  input  s2,
  input  s3,
  output arrive
);

  wire not_1_out, not_2_out;

  not not_1 (not_1_out, s2);
  not not_2 (not_2_out, s3);
  and and_1 (arrive, s1, not_1_out, not_2_out);
endmodule
