// Logisim project 字符自动机.circ as structural Verilog: 3 circuits, main circuit main
module main (
  input  [1:0] in,
  input  rst,
  output [1:0] out
);

  wire clk;
  wire [2:0] multiplexer_1_out, now, pre;

  Clock clock_1 (.out(clk));
  \状态转移  \u_状态转移_1  (
    .pre1(pre[2]), .pre2(pre[1]), .pre3(pre[0]), .in1(in[1]), .in2(in[0]), .now1(now[2]), .now2(now[1]),
    .now3(now[0]));
  \输出  \u_输出_1  (.pre1(pre[2]), .pre2(pre[1]), .pre3(pre[0]), .in1(in[1]), .in2(in[0]), .out1(out[1]), .out2(out[0]));
  // Probe on multiplexer_1_out
  Multiplexer #(.width(3)) multiplexer_1 (.in0(now), .in1(3'b000), .out(multiplexer_1_out), .sel(rst));  // open: en
  Register #(.width(3)) register_1 (.D(multiplexer_1_out), .Q(pre), .clk(clk));  // open: en, clr
endmodule

module \状态转移  (
  input  pre1,
  input  pre2,
  input  pre3,
  input  in1,
  input  in2,
  output now1,
  output now2,
  output now3
);

  wire and_1_out, and_2_out, and_3_out, and_4_out, and_5_out, and_6_out, and_7_out, not_1_out, not_2_out,
       not_3_out, not_4_out, not_5_out, not_6_out, not_7_out, not_8_out, not_9_out, not_10_out;

  not not_1 (not_1_out, pre1);
  not not_2 (not_2_out, pre3);
  not not_3 (not_3_out, pre2);
  not not_4 (not_4_out, in1);
  not not_5 (not_5_out, in2);
  not not_6 (not_6_out, pre1);
  not not_7 (not_7_out, pre3);
  not not_8 (not_8_out, in1);
  not not_9 (not_9_out, pre1);
  not not_10 (not_10_out, pre3);
  and and_1 (and_1_out, not_1_out, pre2, not_2_out, in1);
  and and_2 (and_2_out, pre2, pre3, in2);
  and and_3 (and_3_out, pre1, pre3, in2);
  and and_4 (and_4_out, not_3_out, pre3, not_4_out, not_5_out);
  and and_5 (and_5_out, not_6_out, pre2, not_7_out, in2);
  and and_6 (and_6_out, pre1, pre3, not_8_out);
  and and_7 (and_7_out, not_9_out, pre2, not_10_out, in2);
  or or_1 (now1, and_1_out, and_2_out, and_3_out);
  or or_2 (now2, and_4_out, and_5_out, and_6_out);
  or or_3 (now3, in1, and_7_out);
endmodule

module \输出  (
  input  pre1,
  input  pre2,
  input  pre3,
  input  in1,
  input  in2,
  output out1,
  output out2
);

  wire not_1_out, not_2_out, not_3_out, not_4_out;

  not not_1 (not_1_out, pre2);
  not not_2 (not_2_out, in1);
  not not_3 (not_3_out, pre1);
  not not_4 (not_4_out, in1);
  and and_1 (out1, pre1, not_1_out, pre3, not_2_out, in2);
  and and_2 (out2, not_3_out, pre2, pre3, not_4_out, in2);
endmodule
