// Logisim project 投票.circ as structural Verilog: 2 circuits, main circuit main
module main (
  input  [1:0] \组长 ,
  input  [1:0] a,
  input  [1:0] b,
  input  [1:0] c,
  output out_5
);

  wire comparator_1_gt, decoder_1_out2;
  wire [2:0] \反对_out_6 , \同意_out_6 ;

  // Probe on \同意_out_6 
  \计数器  \u_同意  (.z(\组长 ), .a(a), .b(b), .c(c), .\常数 (2'b11), .out_6(\同意_out_6 ));
  // Probe on \反对_out_6 
  \计数器  \u_反对  (.z(\组长 ), .a(a), .b(b), .c(c), .\常数 (2'b00), .out_6(\反对_out_6 ));
  Comparator #(.width(3), .mode("unsigned")) comparator_1 (
    .a(\同意_out_6 ), .b(\反对_out_6 ), .gt(comparator_1_gt));  // open: eq, lt
  Decoder #(.select(2)) decoder_1 (.out2(decoder_1_out2), .sel(\组长 ));  // open: out0, out1, out3, en
  Multiplexer multiplexer_1 (.in0(comparator_1_gt), .in1(1'b0), .out(out_5), .sel(decoder_1_out2));  // open: en

  // Other names for the same wires on the sheet: z[1:0] = \组长 
endmodule

module \计数器  (
  input  [1:0] z,
  input  [1:0] a,
  input  [1:0] b,
  input  [1:0] c,
  input  [1:0] \常数 ,
  output [2:0] out_6
);

  wire comparator_1_eq, comparator_2_eq, comparator_3_eq, comparator_4_eq;
  wire [2:0] adder_1_out, adder_2_out, bit_extender_1_out, bit_extender_2_out, bit_extender_3_out,
       bit_extender_4_out;

  Comparator #(.width(2), .mode("unsigned")) comparator_1 (.a(z), .b(\常数 ), .eq(comparator_1_eq));  // open: gt, lt
  assign bit_extender_1_out = {{2{1'b0}}, comparator_1_eq};  // Bit_Extender bit_extender_1
  Comparator #(.width(2), .mode("unsigned")) comparator_2 (.a(a), .b(\常数 ), .eq(comparator_2_eq));  // open: gt, lt
  assign bit_extender_2_out = {{2{1'b0}}, comparator_2_eq};  // Bit_Extender bit_extender_2
  assign bit_extender_3_out = {{2{1'b0}}, comparator_3_eq};  // Bit_Extender bit_extender_3
  Comparator #(.width(2), .mode("unsigned")) comparator_3 (.a(b), .b(\常数 ), .eq(comparator_3_eq));  // open: gt, lt
  assign bit_extender_4_out = {{2{1'b0}}, comparator_4_eq};  // Bit_Extender bit_extender_4
  Comparator #(.width(2), .mode("unsigned")) comparator_4 (.a(c), .b(\常数 ), .eq(comparator_4_eq));  // open: gt, lt
  Adder #(.width(3)) adder_1 (.a(bit_extender_1_out), .b(bit_extender_2_out), .out(adder_1_out));  // open: cin, cout
  Adder #(.width(3)) adder_2 (.a(bit_extender_3_out), .b(bit_extender_4_out), .out(adder_2_out));  // open: cin, cout
  Adder #(.width(3)) adder_3 (.a(adder_1_out), .b(adder_2_out), .out(out_6));  // open: cin, cout
endmodule
