// Logisim project ALU.circ as structural Verilog: 1 circuit, main circuit ALU
module ALU (
  input  [31:0] A,
  input  [31:0] B,
  input  [2:0] ALUOp,
  output Zero,
  output LessZero,
  output [31:0] C
);

  wire [31:0] add, \or , sub;

  Adder #(.width(32)) adder_1 (.a(A), .b(B), .out(add));  // open: cin, cout
  Subtractor #(.width(32)) subtractor_1 (.a(A), .b(B), .out(sub));  // open: bin, bout
  assign \or  = A | B;  // OR_Gate or_1, 32 bits wide
  Comparator #(.width(32), .mode("unsigned")) comparator_1 (
    .a(sub), .b({32{1'b0}}), .eq(Zero), .lt(LessZero));  // open: gt
  Multiplexer #(.select(3), .width(32)) multiplexer_1 (
    .in0(add), .in1(sub), .in2(\or ), .in3({B[15:0], {16{1'b0}}}), .out(C), .sel(ALUOp));  // open: in4, in5, in6, in7, en

  // Other names for the same wires on the sheet: lui[31:16] = B[15:0]
endmodule
