// Logisim project CTRL.circ as structural Verilog: 3 circuits, main circuit CTRL
module CTRL (
  input  [5:0] opcode,
  input  [5:0] funct,
  output [1:0] NPCOp,
  output RegWE,
  output [3:0] ALUOp,
  output DmWE,
  output [1:0] EXTOp,
  output RegA3Sel,
  output ALUBSel,
  output RegWDSel
);

  wire and_1_add, and_1_beq, and_1_lui, and_1_lw, and_1_ori, and_1_sub, and_1_sw;

  AND and_1 (
    .opcode(opcode), .funct(funct), .add(and_1_add), .sub(and_1_sub), .ori(and_1_ori), .lw(and_1_lw),
    .sw(and_1_sw), .lui(and_1_lui), .beq(and_1_beq));  // open: nop
  OR or_1 (
    .add(and_1_add), .sub(and_1_sub), .ori(and_1_ori), .lw(and_1_lw), .sw(and_1_sw), .lui(and_1_lui),
    .beq(and_1_beq), .NPCOp(NPCOp), .RegWE(RegWE), .ALUOp(ALUOp), .DmWE(DmWE), .EXTOp(EXTOp),
    .RegA3Sel(RegA3Sel), .ALUBSel(ALUBSel), .RegWDSel(RegWDSel));
endmodule

module AND (
  input  [5:0] opcode,
  input  [5:0] funct,
  output nop,
  output add,
  output sub,
  output ori,
  output lw,
  output sw,
  output lui,
  output beq
);

  wire and_1_out, and_2_out, and_3_out, and_4_out, and_5_out, and_6_out, not_1_out, not_2_out, not_3_out,
       not_4_out, not_5_out, not_6_out, not_7_out, not_8_out, not_9_out, not_10_out, not_11_out, not_12_out,
       not_13_out, not_14_out, not_15_out, not_16_out, not_17_out, not_18_out, not_19_out, not_20_out,
       not_21_out, not_22_out, not_23_out, not_24_out, not_25_out, not_26_out, not_27_out, not_28_out,
       not_29_out, not_30_out, not_31_out, not_32_out, not_33_out, not_34_out, not_35_out, not_36_out,
       not_37_out, not_38_out, not_39_out, not_40_out, not_41_out, not_42_out, not_43_out, not_44_out,
       not_45_out, not_46_out, not_47_out, not_48_out;

  not not_1 (not_1_out, opcode[5]);
  not not_2 (not_2_out, opcode[4]);
  not not_3 (not_3_out, opcode[3]);
  not not_4 (not_4_out, opcode[2]);
  not not_5 (not_5_out, opcode[1]);
  not not_6 (not_6_out, opcode[0]);
  not not_7 (not_7_out, funct[5]);
  not not_8 (not_8_out, funct[4]);
  not not_9 (not_9_out, funct[3]);
  not not_10 (not_10_out, funct[2]);
  not not_11 (not_11_out, funct[1]);
  not not_12 (not_12_out, funct[0]);
  not not_13 (not_13_out, opcode[5]);
  not not_14 (not_14_out, opcode[4]);
  not not_15 (not_15_out, opcode[3]);
  not not_16 (not_16_out, opcode[2]);
  not not_17 (not_17_out, opcode[1]);
  not not_18 (not_18_out, opcode[0]);
  not not_19 (not_19_out, funct[4]);
  not not_20 (not_20_out, funct[3]);
  not not_21 (not_21_out, funct[2]);
  not not_22 (not_22_out, funct[1]);
  not not_23 (not_23_out, funct[0]);
  not not_24 (not_24_out, opcode[5]);
  not not_25 (not_25_out, opcode[4]);
  not not_26 (not_26_out, opcode[3]);
  not not_27 (not_27_out, opcode[2]);
  not not_28 (not_28_out, opcode[1]);
  not not_29 (not_29_out, opcode[0]);
  not not_30 (not_30_out, funct[4]);
  not not_31 (not_31_out, funct[3]);
  not not_32 (not_32_out, funct[2]);
  not not_33 (not_33_out, funct[0]);
  not not_34 (not_34_out, opcode[5]);
  not not_35 (not_35_out, opcode[4]);
  not not_36 (not_36_out, opcode[1]);
  not not_37 (not_37_out, opcode[4]);
  not not_38 (not_38_out, opcode[3]);
  not not_39 (not_39_out, opcode[2]);
  not not_40 (not_40_out, opcode[4]);
  not not_41 (not_41_out, opcode[2]);
  not not_42 (not_42_out, opcode[5]);
  not not_43 (not_43_out, opcode[4]);
  not not_44 (not_44_out, opcode[5]);
  not not_45 (not_45_out, opcode[4]);
  not not_46 (not_46_out, opcode[3]);
  not not_47 (not_47_out, opcode[1]);
  not not_48 (not_48_out, opcode[0]);
  and and_1 (and_1_out, not_1_out, not_2_out, not_3_out, not_4_out, not_5_out, not_6_out);
  and and_2 (and_2_out, not_7_out, not_8_out, not_9_out, not_10_out, not_11_out, not_12_out);
  and and_3 (and_3_out, not_13_out, not_14_out, not_15_out, not_16_out, not_17_out, not_18_out);
  and and_4 (and_4_out, funct[5], not_19_out, not_20_out, not_21_out, not_22_out, not_23_out);
  and and_5 (and_5_out, not_24_out, not_25_out, not_26_out, not_27_out, not_28_out, not_29_out);
  and and_6 (and_6_out, funct[5], not_30_out, not_31_out, not_32_out, funct[1], not_33_out);
  and and_7 (ori, not_34_out, not_35_out, opcode[3], opcode[2], not_36_out, opcode[0]);
  and and_8 (lw, opcode[5], not_37_out, not_38_out, not_39_out, opcode[1], opcode[0]);
  and and_9 (sw, opcode[5], not_40_out, opcode[3], not_41_out, opcode[1], opcode[0]);
  and and_10 (lui, not_42_out, not_43_out, opcode[3], opcode[2], opcode[1], opcode[0]);
  and and_11 (beq, not_44_out, not_45_out, not_46_out, opcode[2], not_47_out, not_48_out);
  and and_12 (nop, and_1_out, and_2_out);
  and and_13 (add, and_3_out, and_4_out);
  and and_14 (sub, and_5_out, and_6_out);

  // Other names for the same wires on the sheet: f0 = funct[0]; f1 = funct[1]; f2 = funct[2]; f3 = funct[3];
  //   f4 = funct[4]; f5 = funct[5]; op0 = opcode[0]; op1 = opcode[1]; op2 = opcode[2]; op3 = opcode[3];
  //   op4 = opcode[4]; op5 = opcode[5]
endmodule

module OR (
  input  add,
  input  sub,
  input  ori,
  input  lw,
  input  sw,
  input  lui,
  input  beq,
  output [1:0] NPCOp,
  output RegWE,
  output [3:0] ALUOp,
  output DmWE,
  output [1:0] EXTOp,
  output RegA3Sel,
  output ALUBSel,
  output RegWDSel
);

  buf or_1 (NPCOp[1], 1'b0);  // OR_Gate
  buf or_2 (NPCOp[0], beq);  // OR_Gate
  or or_3 (RegWE, add, sub, ori, lw, lui);
  buf or_4 (ALUOp[3], 1'b0);  // OR_Gate
  buf or_5 (ALUOp[2], 1'b0);  // OR_Gate
  or or_6 (ALUOp[1], ori, lui);
  or or_7 (ALUOp[0], sub, lui, beq);
  buf or_8 (DmWE, sw);  // OR_Gate
  buf or_9 (EXTOp[1], 1'b0);  // OR_Gate
  or or_10 (EXTOp[0], lw, sw);
  or or_11 (RegA3Sel, ori, lw, lui);
  or or_12 (ALUBSel, ori, lw, lui, sw);
  or or_13 (RegWDSel, add, sub, lw);
endmodule
