// Logisim project DM.circ as structural Verilog: 1 circuit, main circuit DM
module DM (
  input  clk,
  input  rst,
  input  [31:0] A,
  input  [31:0] WD,
  input  WE,
  output [31:0] RD
);

  // Probe on A[13:2]
  RAM #(.addrWidth(12), .dataWidth(32), .bus("separate")) ram_1 (
    .addr(A[13:2]), .din(WD), .data(RD), .str(WE), .clk(clk), .clr(rst));  // open: sel, ld
endmodule
