// Logisim project EXT.circ as structural Verilog: 1 circuit, main circuit EXT
module EXT (
  input  [1:0] EXTOp,
  input  [15:0] Input,
  output [31:0] Output
);

  wire [31:0] bit_extender_1_out, bit_extender_2_out;

  assign bit_extender_1_out = {{16{1'b0}}, Input};  // Bit_Extender bit_extender_1
  assign bit_extender_2_out = {{16{Input[15]}}, Input};  // Bit_Extender bit_extender_2
  Multiplexer #(.select(2), .width(32)) multiplexer_1 (
    .in0(bit_extender_1_out), .in1(bit_extender_2_out), .out(Output), .sel(EXTOp));  // open: in2, in3, en

  // Other names for the same wires on the sheet: In[15:0] = Input; Op[1:0] = EXTOp; Out[31:0] = Output
endmodule
