// Logisim project IFU.circ as structural Verilog: 4 circuits, main circuit IFU
module IFU (
  input  clk,
  input  rst,
  input  [25:0] imm26_16,
  input  [31:0] A32,
  input  [1:0] NPCOp,
  input  Zero,
  input  LessZero,
  output [31:0] out_8
);

  wire [31:0] NPC, pc_1_do;

  PC pc_1 (.clk(clk), .rst(rst), .DI(NPC), .DO(pc_1_do));
  // Probe on pc_1_do
  NPC npc_1 (.PC(pc_1_do), .imm26_16(imm26_16), .A32(A32), .NPCOp(NPCOp), .Zero(Zero), .NPC(NPC));  // open: LessZero
  // Probe on NPC
  IM im_1 (.PC(pc_1_do), .Instr(out_8));

  // Other names for the same wires on the sheet: Instr[31:0] = out_8
endmodule

module NPC (
  input  [1:0] NPCOp,
  input  Zero,
  input  LessZero,
  input  [31:0] PC,
  input  [25:0] imm26_16,
  input  [31:0] A32,
  output [31:0] NPC
);

  wire [31:0] adder_2_out, beq, bit_extender_1_out, jal, normal;

  // Probe on {imm26_16, 2'b00}
  assign bit_extender_1_out = {{4{imm26_16[25]}}, {imm26_16, 2'b00}};  // Bit_Extender bit_extender_1
  assign jal = {{4{1'b0}}, {imm26_16, 2'b00}};  // Bit_Extender bit_extender_2
  Adder #(.width(32)) adder_1 (.a(PC), .b(32'h4), .out(normal));  // open: cin, cout
  Adder #(.width(32)) adder_2 (.a(normal), .b(bit_extender_1_out), .out(adder_2_out));  // open: cin, cout
  Multiplexer #(.width(32)) multiplexer_1 (.in0(adder_2_out), .in1(normal), .out(beq), .sel(Zero));  // open: en
  Multiplexer #(.select(2), .width(32)) multiplexer_2 (
    .in0(normal), .in1(beq), .in2(A32), .in3(jal), .out(NPC), .sel(NPCOp));  // open: en
endmodule

module PC (
  input  clk,
  input  rst,
  input  [31:0] DI,
  output [31:0] DO
);

  wire comparator_1_eq;
  wire [31:0] adder_1_out, register_1_q;

  Register #(.width(32)) register_1 (.D(DI), .Q(register_1_q), .clk(clk), .clr(rst));  // open: en
  Comparator #(.width(32), .mode("unsigned")) comparator_1 (
    .a(register_1_q), .b({32{1'b0}}), .eq(comparator_1_eq));  // open: gt, lt
  Adder #(.width(32)) adder_1 (.a(register_1_q), .b(32'h3000), .out(adder_1_out));  // open: cin, cout
  Multiplexer #(.width(32)) multiplexer_1 (
    .in0(register_1_q), .in1(adder_1_out), .out(DO), .sel(comparator_1_eq));  // open: en

  // Other names for the same wires on the sheet: in[31:0] = DI; out[31:0] = DO
endmodule

module IM (
  input  [31:0] PC,
  output [31:0] Instr
);

  ROM #(.addrWidth(12), .dataWidth(32)) rom_1 (.addr(PC[13:2]), .data(Instr));  // open: sel
endmodule
