// Logisim project cpu.circ as structural Verilog: 12 circuits, main circuit main
module main (
  input  rst,
  output [31:0] Instr,
  output [31:0] pc,
  output RegWrite,
  output [4:0] RegAddr,
  output [31:0] RegData,
  output MemWrite,
  output [31:0] MemAddr,
  output [31:0] MemData
);

  wire ALUBSel, clk, ctrland_1_add, ctrland_1_beq, ctrland_1_jal, ctrland_1_jr, ctrland_1_lui, ctrland_1_lw,
       ctrland_1_ori, ctrland_1_sub, ctrland_1_sw, EXTOp, LessZero, Zero;
  wire [1:0] NPCOp, RegA3Sel, RegWDSel;
  wire [3:0] ALUOp;
  wire [4:0] _15_11, _20_16, _25_21;
  wire [5:0] funct, opcode;
  wire [15:0] imm16;
  wire [25:0] imm26;
  wire [31:0] DmRD, EXTimm, multiplexer_3_out, PC_4, RD1;

  Clock clock_1 (.out(clk));
  Multiplexer #(.select(2), .width(5)) multiplexer_1 (
    .in0(_15_11), .in1(_20_16), .in2({5{1'b1}}), .out(RegAddr), .sel(RegA3Sel));  // open: in3, en
  IFU ifu_1 (
    .imm26(imm26), .RA(RD1), .NPCOp(NPCOp), .Zero(Zero), .LessZero(LessZero), .Instr(Instr), .clk(clk),
    .rst(rst), .PC(pc), .imm16(imm16), .PC_4(PC_4));
  ctrlAND ctrland_1 (
    .opcode(opcode), .funct(funct), .add(ctrland_1_add), .sub(ctrland_1_sub), .ori(ctrland_1_ori),
    .lw(ctrland_1_lw), .sw(ctrland_1_sw), .lui(ctrland_1_lui), .beq(ctrland_1_beq), .jr(ctrland_1_jr),
    .jal(ctrland_1_jal));  // open: nop
  Multiplexer #(.select(2), .width(32)) multiplexer_2 (
    .in0(MemAddr), .in1(DmRD), .in2(PC_4), .out(RegData), .sel(RegWDSel));  // open: in3, en
  // Probe on ALUOp
  // Probe on NPCOp
  ctrlOR ctrlor_1 (
    .add(ctrland_1_add), .sub(ctrland_1_sub), .ori(ctrland_1_ori), .lw(ctrland_1_lw), .sw(ctrland_1_sw),
    .lui(ctrland_1_lui), .beq(ctrland_1_beq), .NPCOp(NPCOp), .RegWE(RegWrite), .ALUOp(ALUOp),
    .DmWE(MemWrite), .EXTOp(EXTOp), .RegA3Sel(RegA3Sel), .ALUBSel(ALUBSel), .RegWDSel(RegWDSel),
    .jr(ctrland_1_jr), .jal(ctrland_1_jal));
  // Probe on RD1
  GRF grf_1 (
    .A1(_25_21), .A2(_20_16), .A3(RegAddr), .WD(RegData), .RD1(RD1), .RD2(MemData), .clk(clk), .reset(rst),
    .WE(RegWrite));
  // Probe on MemData
  // Probe on imm26
  // Probe on imm16
  splitter splitter_1 (
    .Instr(Instr), .opcode(opcode), .funct(funct), .rs(_25_21), .rt(_20_16), .rd(_15_11), .imm16(imm16),
    .imm26(imm26));
  EXT ext_1 (.Input(imm16), .Output(EXTimm), .EXTOp(EXTOp));
  Multiplexer #(.width(32)) multiplexer_3 (
    .in0(MemData), .in1(EXTimm), .out(multiplexer_3_out), .sel(ALUBSel));  // open: en
  ALU alu_1 (.A(RD1), .B(multiplexer_3_out), .C(MemAddr), .ALUOp(ALUOp), .Zero(Zero), .LessZero(LessZero));
  DM dm_1 (.A(MemAddr), .WD(MemData), .WE(MemWrite), .RD(DmRD), .clk(clk), .rst(rst));

  // Other names for the same wires on the sheet: ALUOutput[31:0] = MemAddr; DmWE = MemWrite; RD2[31:0] = MemData;
  //   RegWE = RegWrite
endmodule

module IFU (
  input  clk,
  input  rst,
  input  [15:0] imm16,
  input  [25:0] imm26,
  input  [31:0] RA,
  input  [1:0] NPCOp,
  input  Zero,
  input  LessZero,
  output [31:0] Instr,
  output [31:0] PC,
  output [31:0] PC_4
);

  wire [31:0] NPC;

  PC pc_1 (.clk(clk), .rst(rst), .DI(NPC), .DO(PC));
  // Probe on PC
  NPC npc_1 (
    .PC(PC), .imm16(imm16), .imm26(imm26), .A32(RA), .NPC(NPC), .PC_4(PC_4), .NPCOp(NPCOp), .Zero(Zero),
    .LessZero(LessZero));
  // Probe on NPC
  IM im_1 (.PC(PC), .Instr(Instr));

  // Other names for the same wires on the sheet: A32[31:0] = RA
endmodule

module PC (
  input  clk,
  input  rst,
  input  [31:0] DI,
  output [31:0] DO
);

  wire comparator_1_eq;
  wire [31:0] register_1_q;

  Register #(.width(32)) register_1 (.D(DI), .Q(register_1_q), .clk(clk), .clr(rst));  // open: en
  Comparator #(.width(32), .mode("unsigned")) comparator_1 (
    .a({32{1'b0}}), .b(register_1_q), .eq(comparator_1_eq));  // open: gt, lt
  Multiplexer #(.width(32)) multiplexer_1 (
    .in0(register_1_q), .in1(32'h3000), .out(DO), .sel(comparator_1_eq));  // open: en

  // Other names for the same wires on the sheet: in[31:0] = DI; out[31:0] = DO
endmodule

module NPC (
  input  [1:0] NPCOp,
  input  Zero,
  input  LessZero,
  input  [31:0] PC,
  input  [15:0] imm16,
  input  [25:0] imm26,
  input  [31:0] A32,
  output [31:0] NPC,
  output [31:0] PC_4
);

  wire [31:0] adder_2_out, beq, bit_extender_1_out;

  // Probe on {imm16, 2'b00}
  assign bit_extender_1_out = {{14{imm16[15]}}, {imm16, 2'b00}};  // Bit_Extender bit_extender_1
  Adder #(.width(32)) adder_1 (.a(PC), .b(32'h4), .out(PC_4));  // open: cin, cout
  Adder #(.width(32)) adder_2 (.a(PC_4), .b(bit_extender_1_out), .out(adder_2_out));  // open: cin, cout
  Multiplexer #(.width(32)) multiplexer_1 (.in0(PC_4), .in1(adder_2_out), .out(beq), .sel(Zero));  // open: en
  Multiplexer #(.select(2), .width(32)) multiplexer_2 (
    .in0(PC_4), .in1(beq), .in2(A32), .in3({PC[31:28], imm26, 2'b00}), .out(NPC), .sel(NPCOp));  // open: en

  // Other names for the same wires on the sheet: jal[31:2] = {PC[31:28], imm26}; PC_31_28[3:0] = PC[31:28];
  //   normal[31:0] = PC_4
endmodule

module IM (
  input  [31:0] PC,
  output [31:0] Instr
);

  wire [11:0] subtractor_1_out;

  Subtractor #(.width(12)) subtractor_1 (.a(PC[13:2]), .b(12'hc00), .out(subtractor_1_out));  // open: bin, bout
  ROM #(.addrWidth(12), .dataWidth(32)) rom_1 (.addr(subtractor_1_out), .data(Instr));  // open: sel

  // Notes on the sheet:
  //   contents of rom_1 (hex, n*v repeats v):
  //   341c0000 341d0000 34013456 210820 8c010004 ac010004 3c027878 411822 3c051234 34040005 0 ac85ffff
  //   8c83ffff 10650001 1000000d 34670404 10e3000b 0 3c087777 3508ffff 80022 34001100 e65020 34080000
  //   34090001 340a0001 10a4020 1109fffe 1000ffff
endmodule

module GRF (
  input  clk,
  input  reset,
  input  WE,
  input  [4:0] A1,
  input  [4:0] A2,
  input  [4:0] A3,
  input  [31:0] WD,
  output [31:0] RD1,
  output [31:0] RD2
);

  wire [31:0] _00_q, i00, i01, i02, i03, i04, i05, i06, i07, i08, i09, i10, i11, i12, i13, i14, i15, i16,
       i17, i18, i19, i20, i21, i22, i23, i24, i25, i26, i27, i28, i29, i30, i31, o00, o01, o02, o03, o04,
       o05, o06, o07, o08, o09, o10, o11, o12, o13, o14, o15, o16, o17, o18, o19, o20, o21, o22, o23, o24,
       o25, o26, o27, o28, o29, o30, o31;

  Demultiplexer #(.select(5), .width(32), .tristate("true")) demultiplexer_1 (
    .out0(i00), .out1(i01), .out2(i02), .out3(i03), .out4(i04), .out5(i05), .out6(i06), .out7(i07),
    .out8(i08), .out9(i09), .out10(i10), .out11(i11), .out12(i12), .out13(i13), .out14(i14), .out15(i15),
    .out16(i16), .out17(i17), .out18(i18), .out19(i19), .out20(i20), .out21(i21), .out22(i22), .out23(i23),
    .out24(i24), .out25(i25), .out26(i26), .out27(i27), .out28(i28), .out29(i29), .out30(i30), .out31(i31),
    .in(WD), .sel(A3), .en(WE));
  Multiplexer #(.select(5), .width(32)) multiplexer_1 (
    .in0(o00), .in1(o01), .in2(o02), .in3(o03), .in4(o04), .in5(o05), .in6(o06), .in7(o07), .in8(o08),
    .in9(o09), .in10(o10), .in11(o11), .in12(o12), .in13(o13), .in14(o14), .in15(o15), .in16(o16),
    .in17(o17), .in18(o18), .in19(o19), .in20(o20), .in21(o21), .in22(o22), .in23(o23), .in24(o24),
    .in25(o25), .in26(o26), .in27(o27), .in28(o28), .in29(o29), .in30(o30), .in31(o31), .out(RD1), .sel(A1));  // open: en
  Multiplexer #(.select(5), .width(32)) multiplexer_2 (
    .in0(o00), .in1(o01), .in2(o02), .in3(o03), .in4(o04), .in5(o05), .in6(o06), .in7(o07), .in8(o08),
    .in9(o09), .in10(o10), .in11(o11), .in12(o12), .in13(o13), .in14(o14), .in15(o15), .in16(o16),
    .in17(o17), .in18(o18), .in19(o19), .in20(o20), .in21(o21), .in22(o22), .in23(o23), .in24(o24),
    .in25(o25), .in26(o26), .in27(o27), .in28(o28), .in29(o29), .in30(o30), .in31(o31), .out(RD2), .sel(A2));  // open: en
  Register #(.width(32)) _00 (.D(i00), .en(WE), .Q(_00_q), .clk(clk), .clr(reset));
  Register #(.width(32)) _04 (.D(i04), .en(WE), .Q(o04), .clk(clk), .clr(reset));
  Register #(.width(32)) _08 (.D(i08), .en(WE), .Q(o08), .clk(clk), .clr(reset));
  Register #(.width(32)) _12 (.D(i12), .en(WE), .Q(o12), .clk(clk), .clr(reset));
  Register #(.width(32)) _16 (.D(i16), .en(WE), .Q(o16), .clk(clk), .clr(reset));
  Register #(.width(32)) _20 (.D(i20), .en(WE), .Q(o20), .clk(clk), .clr(reset));
  Register #(.width(32)) _24 (.D(i24), .en(WE), .Q(o24), .clk(clk), .clr(reset));
  Register #(.width(32)) _28 (.D(i28), .en(WE), .Q(o28), .clk(clk), .clr(reset));
  // Probe on o01
  assign o00 = {32{1'b0}} & _00_q;  // AND_Gate and_1, 32 bits wide
  Register #(.width(32)) _01 (.D(i01), .en(WE), .Q(o01), .clk(clk), .clr(reset));
  Register #(.width(32)) _05 (.D(i05), .en(WE), .Q(o05), .clk(clk), .clr(reset));
  Register #(.width(32)) _09 (.D(i09), .en(WE), .Q(o09), .clk(clk), .clr(reset));
  Register #(.width(32)) _13 (.D(i13), .en(WE), .Q(o13), .clk(clk), .clr(reset));
  Register #(.width(32)) _17 (.D(i17), .en(WE), .Q(o17), .clk(clk), .clr(reset));
  Register #(.width(32)) _21 (.D(i21), .en(WE), .Q(o21), .clk(clk), .clr(reset));
  Register #(.width(32)) _25 (.D(i25), .en(WE), .Q(o25), .clk(clk), .clr(reset));
  Register #(.width(32)) _29 (.D(i29), .en(WE), .Q(o29), .clk(clk), .clr(reset));
  Register #(.width(32)) _02 (.D(i02), .en(WE), .Q(o02), .clk(clk), .clr(reset));
  Register #(.width(32)) _06 (.D(i06), .en(WE), .Q(o06), .clk(clk), .clr(reset));
  Register #(.width(32)) _10 (.D(i10), .en(WE), .Q(o10), .clk(clk), .clr(reset));
  Register #(.width(32)) _14 (.D(i14), .en(WE), .Q(o14), .clk(clk), .clr(reset));
  Register #(.width(32)) _18 (.D(i18), .en(WE), .Q(o18), .clk(clk), .clr(reset));
  Register #(.width(32)) _22 (.D(i22), .en(WE), .Q(o22), .clk(clk), .clr(reset));
  Register #(.width(32)) _26 (.D(i26), .en(WE), .Q(o26), .clk(clk), .clr(reset));
  Register #(.width(32)) _30 (.D(i30), .en(WE), .Q(o30), .clk(clk), .clr(reset));
  Register #(.width(32)) _03 (.D(i03), .en(WE), .Q(o03), .clk(clk), .clr(reset));
  Register #(.width(32)) _07 (.D(i07), .en(WE), .Q(o07), .clk(clk), .clr(reset));
  Register #(.width(32)) _11 (.D(i11), .en(WE), .Q(o11), .clk(clk), .clr(reset));
  Register #(.width(32)) _15 (.D(i15), .en(WE), .Q(o15), .clk(clk), .clr(reset));
  Register #(.width(32)) _19 (.D(i19), .en(WE), .Q(o19), .clk(clk), .clr(reset));
  Register #(.width(32)) _23 (.D(i23), .en(WE), .Q(o23), .clk(clk), .clr(reset));
  Register #(.width(32)) _27 (.D(i27), .en(WE), .Q(o27), .clk(clk), .clr(reset));
  Register #(.width(32)) _31 (.D(i31), .en(WE), .Q(o31), .clk(clk), .clr(reset));

  // Other names for the same wires on the sheet: rst = reset
endmodule

module ALU (
  input  [31:0] A,
  input  [31:0] B,
  input  [3:0] ALUOp,
  output Zero,
  output LessZero,
  output [31:0] C
);

  wire [31:0] add, \or , sub;

  Adder #(.width(32)) adder_1 (.a(A), .b(B), .out(add));  // open: cin, cout
  Subtractor #(.width(32)) subtractor_1 (.a(A), .b(B), .out(sub));  // open: bin, bout
  assign \or  = A | B;  // OR_Gate or_1, 32 bits wide
  Comparator #(.width(32), .mode("unsigned")) comparator_1 (
    .a(sub), .b({32{1'b0}}), .eq(Zero), .lt(LessZero));  // open: gt
  Multiplexer #(.select(4), .width(32)) multiplexer_1 (
    .in0(add), .in1(sub), .in2(\or ), .in3({B[15:0], {16{1'b0}}}), .out(C), .sel(ALUOp));  // open: in4, in5, in6, in7, in8, in9, in10, in11, in12, in13, in14, in15, en

  // Other names for the same wires on the sheet: lui[31:16] = B[15:0]
endmodule

module DM (
  input  clk,
  input  rst,
  input  [31:0] A,
  input  [31:0] WD,
  input  WE,
  output [31:0] RD
);

  // Probe on A[13:2]
  RAM #(.addrWidth(12), .dataWidth(32), .bus("separate")) ram_1 (
    .addr(A[13:2]), .din(WD), .data(RD), .str(WE), .clk(clk), .clr(rst));  // open: sel, ld
endmodule

module EXT (
  input  EXTOp,
  input  [15:0] Input,
  output [31:0] Output
);

  wire [31:0] bit_extender_1_out, bit_extender_2_out;

  assign bit_extender_1_out = {{16{1'b0}}, Input};  // Bit_Extender bit_extender_1
  assign bit_extender_2_out = {{16{Input[15]}}, Input};  // Bit_Extender bit_extender_2
  Multiplexer #(.width(32)) multiplexer_1 (
    .in0(bit_extender_1_out), .in1(bit_extender_2_out), .out(Output), .sel(EXTOp));  // open: en

  // Other names for the same wires on the sheet: In[15:0] = Input; Op = EXTOp; Out[31:0] = Output
endmodule

module splitter (
  input  [31:0] Instr,
  output [5:0] opcode,
  output [5:0] funct,
  output [4:0] rs,
  output [4:0] rt,
  output [4:0] rd,
  output [15:0] imm16,
  output [25:0] imm26
);


  assign funct = Instr[5:0];
  assign imm16 = Instr[15:0];
  assign imm26 = Instr[25:0];
  assign opcode = Instr[31:26];
  assign rd = Instr[15:11];
  assign rs = Instr[25:21];
  assign rt = Instr[20:16];

  // Other names for the same wires on the sheet: _5_0[5:0] = Instr[5:0]; _10_6[4:0] = Instr[10:6];
  //   _15_11[4:0] = Instr[15:11]; _20_16[4:0] = Instr[20:16]; _25_21[4:0] = Instr[25:21]
endmodule

module ctrlAND (
  input  [5:0] opcode,
  input  [5:0] funct,
  output nop,
  output add,
  output sub,
  output ori,
  output lw,
  output sw,
  output lui,
  output beq,
  output jr,
  output jal
);

  wire and_2_out, and_3_out, and_4_out, and_10_out, not_1_out, not_2_out, not_3_out, not_4_out, not_5_out,
       not_6_out, not_7_out, not_8_out, not_9_out, not_10_out, not_11_out, not_12_out, not_13_out,
       not_14_out, not_15_out, not_16_out, not_17_out, not_18_out, not_19_out, not_20_out, not_21_out,
       not_22_out, not_23_out, not_24_out, not_25_out, not_26_out, not_27_out, not_28_out, not_29_out,
       not_30_out, not_31_out, not_32_out, not_33_out, not_34_out, not_35_out, not_36_out, not_37_out,
       not_38_out, not_39_out, not_40_out, not_41_out, not_42_out, not_43_out, not_44_out, not_45_out,
       special;

  not not_1 (not_1_out, opcode[5]);
  not not_2 (not_2_out, opcode[4]);
  not not_3 (not_3_out, opcode[3]);
  not not_4 (not_4_out, opcode[2]);
  not not_5 (not_5_out, opcode[1]);
  not not_6 (not_6_out, opcode[0]);
  and and_1 (special, not_1_out, not_2_out, not_3_out, not_4_out, not_5_out, not_6_out);
  not not_7 (not_7_out, funct[5]);
  not not_8 (not_8_out, funct[4]);
  not not_9 (not_9_out, funct[3]);
  not not_10 (not_10_out, funct[2]);
  not not_11 (not_11_out, funct[1]);
  not not_12 (not_12_out, funct[0]);
  not not_13 (not_13_out, funct[4]);
  not not_14 (not_14_out, funct[3]);
  not not_15 (not_15_out, funct[2]);
  not not_16 (not_16_out, funct[1]);
  not not_17 (not_17_out, funct[0]);
  not not_18 (not_18_out, funct[4]);
  not not_19 (not_19_out, funct[3]);
  not not_20 (not_20_out, funct[2]);
  not not_21 (not_21_out, funct[0]);
  not not_22 (not_22_out, opcode[5]);
  not not_23 (not_23_out, opcode[4]);
  not not_24 (not_24_out, opcode[1]);
  not not_25 (not_25_out, opcode[4]);
  not not_26 (not_26_out, opcode[3]);
  not not_27 (not_27_out, opcode[2]);
  not not_28 (not_28_out, opcode[4]);
  not not_29 (not_29_out, opcode[2]);
  not not_30 (not_30_out, opcode[5]);
  not not_31 (not_31_out, opcode[4]);
  not not_32 (not_32_out, opcode[5]);
  not not_33 (not_33_out, opcode[4]);
  not not_34 (not_34_out, opcode[3]);
  not not_35 (not_35_out, opcode[1]);
  not not_36 (not_36_out, opcode[0]);
  not not_37 (not_37_out, funct[5]);
  not not_38 (not_38_out, funct[4]);
  not not_39 (not_39_out, funct[2]);
  not not_40 (not_40_out, funct[1]);
  not not_41 (not_41_out, funct[0]);
  not not_42 (not_42_out, opcode[5]);
  not not_43 (not_43_out, opcode[4]);
  not not_44 (not_44_out, opcode[3]);
  not not_45 (not_45_out, opcode[2]);
  and and_2 (and_2_out, not_7_out, not_8_out, not_9_out, not_10_out, not_11_out, not_12_out);
  and and_3 (and_3_out, funct[5], not_13_out, not_14_out, not_15_out, not_16_out, not_17_out);
  and and_4 (and_4_out, funct[5], not_18_out, not_19_out, not_20_out, funct[1], not_21_out);
  and and_5 (ori, not_22_out, not_23_out, opcode[3], opcode[2], not_24_out, opcode[0]);
  and and_6 (lw, opcode[5], not_25_out, not_26_out, not_27_out, opcode[1], opcode[0]);
  and and_7 (sw, opcode[5], not_28_out, opcode[3], not_29_out, opcode[1], opcode[0]);
  and and_8 (lui, not_30_out, not_31_out, opcode[3], opcode[2], opcode[1], opcode[0]);
  and and_9 (beq, not_32_out, not_33_out, not_34_out, opcode[2], not_35_out, not_36_out);
  and and_10 (and_10_out, not_37_out, not_38_out, funct[3], not_39_out, not_40_out, not_41_out);
  and and_11 (jal, not_42_out, not_43_out, not_44_out, not_45_out, opcode[1], opcode[0]);
  and and_12 (nop, special, and_2_out);
  and and_13 (add, special, and_3_out);
  and and_14 (sub, special, and_4_out);
  and and_15 (jr, special, and_10_out);

  // Other names for the same wires on the sheet: f0 = funct[0]; f1 = funct[1]; f2 = funct[2]; f3 = funct[3];
  //   f4 = funct[4]; f5 = funct[5]; op0 = opcode[0]; op1 = opcode[1]; op2 = opcode[2]; op3 = opcode[3];
  //   op4 = opcode[4]; op5 = opcode[5]
endmodule

module ctrlOR (
  input  add,
  input  sub,
  input  ori,
  input  lw,
  input  sw,
  input  lui,
  input  beq,
  input  jr,
  input  jal,
  output [1:0] NPCOp,
  output RegWE,
  output [3:0] ALUOp,
  output DmWE,
  output EXTOp,
  output [1:0] RegA3Sel,
  output ALUBSel,
  output [1:0] RegWDSel
);

  or or_1 (NPCOp[1], jr, jal);
  or or_2 (NPCOp[0], beq, jal);
  or or_3 (RegWE, add, sub, ori, lw, lui, jal);
  buf or_4 (ALUOp[3], 1'b0);  // OR_Gate
  buf or_5 (ALUOp[2], 1'b0);  // OR_Gate
  or or_6 (ALUOp[1], ori, lui);
  or or_7 (ALUOp[0], sub, lui, beq);
  buf or_8 (DmWE, sw);  // OR_Gate
  or or_9 (EXTOp, lw, sw);
  buf or_10 (RegA3Sel[1], jal);  // OR_Gate
  or or_11 (RegA3Sel[0], ori, lw, lui);
  or or_12 (ALUBSel, ori, lw, lui, sw);
  buf or_13 (RegWDSel[1], jal);  // OR_Gate
  buf or_14 (RegWDSel[0], lw);  // OR_Gate
endmodule
