// Logisim project splitter.circ as structural Verilog: 1 circuit, main circuit splitter
module splitter (
  input  [31:0] Instr,
  output [5:0] opcode,
  output [5:0] funct,
  output [4:0] rs,
  output [4:0] rt,
  output [4:0] rd,
  output [15:0] imm16
);


  assign funct = Instr[5:0];
  assign imm16 = Instr[15:0];
  assign opcode = Instr[31:26];
  assign rd = Instr[15:11];
  assign rs = Instr[25:21];
  assign rt = Instr[20:16];

  // Other names for the same wires on the sheet: _20_16[4:0] = Instr[20:16]; _25_21[4:0] = Instr[25:21];
  //   _5_0[5:0] = Instr[5:0]; _10_6[4:0] = Instr[10:6]; _15_11[4:0] = Instr[15:11]
endmodule
