// Logisim project 2^n_mod_5.circ as structural Verilog: 3 circuits, main circuit mod5
module mod5 (
  input  In,
  output s0,
  output s1,
  output s2,
  output s3,
  output s4
);

  wire clock_1_out;
  wire [1:0] t, \状态转移_1_out_3 ;

  \状态转移  \u_状态转移_1  (.in_1(t), .b(In), .out_3(\状态转移_1_out_3 ));
  Register #(.width(2)) register_1 (.D(\状态转移_1_out_3 ), .Q(t), .clk(clock_1_out));  // open: en, clr
  Clock clock_1 (.out(clock_1_out));
  \输出  \u_输出_1  (.in_1(t), .b(In), .s0(s0), .s1(s1), .s2(s2), .s3(s3), .s4(s4));
endmodule

module \状态转移  (
  input  [1:0] in_1,
  input  b,
  output [1:0] out_3
);

  wire and_1_out, and_2_out, and_3_out, and_4_out, and_5_out, and_6_out, not_1_out, not_2_out, not_3_out,
       not_4_out, not_5_out, not_6_out, not_7_out, not_8_out;

  not not_1 (not_1_out, in_1[0]);
  not not_2 (not_2_out, in_1[1]);
  not not_3 (not_3_out, in_1[0]);
  not not_4 (not_4_out, in_1[1]);
  not not_5 (not_5_out, in_1[0]);
  not not_6 (not_6_out, b);
  not not_7 (not_7_out, in_1[1]);
  not not_8 (not_8_out, b);
  and and_1 (and_1_out, not_1_out, in_1[1]);
  or or_1 (out_3[0], and_1_out, and_2_out);
  and and_2 (and_2_out, in_1[0], not_2_out);
  and and_3 (and_3_out, not_3_out, not_4_out, b);
  and and_4 (and_4_out, not_5_out, in_1[1], not_6_out);
  and and_5 (and_5_out, in_1[0], not_7_out, not_8_out);
  and and_6 (and_6_out, in_1[0], in_1[1], b);
  or or_2 (out_3[1], and_3_out, and_4_out, and_5_out, and_6_out);
endmodule

module \输出  (
  input  [1:0] in_1,
  input  b,
  output s0,
  output s1,
  output s2,
  output s3,
  output s4
);

  wire and_1_out, and_2_out, and_3_out, and_4_out, and_5_out, and_6_out, and_7_out, and_8_out, not_1_out,
       not_2_out, not_3_out, not_4_out, not_5_out, not_6_out, not_7_out, not_8_out, not_9_out, not_10_out,
       not_11_out, not_12_out;

  not not_1 (not_1_out, in_1[0]);
  not not_2 (not_2_out, in_1[1]);
  and and_1 (and_1_out, not_1_out, not_2_out, not_3_out);
  not not_3 (not_3_out, b);
  and and_2 (and_2_out, in_1[0], in_1[1], not_4_out);
  not not_4 (not_4_out, b);
  not not_5 (not_5_out, in_1[0]);
  not not_6 (not_6_out, in_1[1]);
  and and_3 (and_3_out, not_5_out, not_6_out, b);
  and and_4 (and_4_out, in_1[0], in_1[1], b);
  not not_7 (not_7_out, in_1[0]);
  and and_5 (and_5_out, not_7_out, in_1[1], b);
  and and_6 (and_6_out, in_1[0], not_8_out, b);
  not not_8 (not_8_out, in_1[1]);
  not not_9 (not_9_out, in_1[0]);
  and and_7 (and_7_out, not_9_out, in_1[1], not_10_out);
  not not_10 (not_10_out, b);
  and and_8 (and_8_out, in_1[0], not_11_out, not_12_out);
  not not_11 (not_11_out, in_1[1]);
  not not_12 (not_12_out, b);
  or or_1 (s1, and_1_out, and_2_out);
  or or_2 (s2, and_3_out, and_4_out);
  or or_3 (s3, and_5_out, and_6_out);
  or or_4 (s4, and_7_out, and_8_out);

  assign s0 = 1'b0;
endmodule
