// Logisim project fibonacci.circ as structural Verilog: 3 circuits, main circuit main
module main (
  input  [2:0] N,
  output [3:0] Nth
);

  wire \计数_out_2 ;
  wire [3:0] \计算_out_2 ;

  \计数  \u_计数  (.in_1(N), .out_2(\计数_out_2 ));
  // Probe on \计算_out_2 
  \计算  \u_计算  (.stop(\计数_out_2 ), .out_2(\计算_out_2 ));
  Multiplexer #(.width(4)) multiplexer_1 (.in0(4'b0000), .in1(\计算_out_2 ), .out(Nth), .sel(\计数_out_2 ));  // open: en
endmodule

module \计算  (
  input  stop,
  output [3:0] out_2
);

  wire clock, enable, init;
  wire [3:0] adder_1_out, multiplexer_1_out, prev;

  Clock clock_1 (.out(clock));
  Counter #(.width(1), .max('h1), .ongoal("stay")) counter_1 (
    .Q(init), .clk(clock));  // open: load, D, count, carry, clr
  not not_1 (enable, stop);
  Multiplexer #(.width(4)) multiplexer_1 (.in0(4'b0001), .in1(out_2), .out(multiplexer_1_out), .sel(init));  // open: en
  Adder #(.width(4)) adder_1 (.a(prev), .b(out_2), .out(adder_1_out));  // open: cin, cout
  Register #(.width(4)) u_prev (.D(multiplexer_1_out), .en(enable), .Q(prev), .clk(clock));  // open: clr
  Register #(.width(4)) now (.D(adder_1_out), .en(enable), .Q(out_2), .clk(clock));  // open: clr

  // Other names for the same wires on the sheet: now[3:0] = out_2
endmodule

module \计数  (
  input  [2:0] in_1,
  output out_2
);

  wire clock;
  wire [3:0] bit_extender_1_out, counter_1_q;

  Clock clock_1 (.out(clock));
  assign bit_extender_1_out = {{1{1'b0}}, in_1};  // Bit_Extender bit_extender_1
  Counter #(.width(4), .max('hf), .ongoal("stay")) counter_1 (
    .Q(counter_1_q), .clk(clock));  // open: load, D, count, carry, clr
  Comparator #(.width(4), .mode("unsigned")) comparator_1 (
    .a(bit_extender_1_out), .b(counter_1_q), .lt(out_2));  // open: gt, eq
endmodule
