// Logisim project sort_4bit.circ as structural Verilog: 4 circuits, main circuit 4bit_sort
module _4bit_sort (
  input  [3:0] A,
  input  [3:0] B,
  input  [3:0] C,
  input  [3:0] D,
  output [3:0] _1,
  output [3:0] _2,
  output [3:0] _3,
  output [3:0] _4
);

  wire [3:0] separated_step_swap_1_a_2, separated_step_swap_1_b_2, separated_step_swap_2_a_2,
       separated_step_swap_2_b_2, separated_step_swap_3_a_2, separated_step_swap_4_a_2,
       separated_step_swap_4_b_2, separated_step_swap_5_a_2;

  separated_step_swap separated_step_swap_1 (
    .a(A), .b(B), .A_2(separated_step_swap_1_a_2), .B_2(separated_step_swap_1_b_2));
  separated_step_swap separated_step_swap_2 (
    .a(separated_step_swap_1_b_2), .b(C), .A_2(separated_step_swap_2_a_2), .B_2(separated_step_swap_2_b_2));
  separated_step_swap separated_step_swap_3 (
    .a(separated_step_swap_2_b_2), .b(D), .A_2(separated_step_swap_3_a_2), .B_2(_4));
  separated_step_swap separated_step_swap_4 (
    .a(separated_step_swap_1_a_2), .b(separated_step_swap_2_a_2), .A_2(separated_step_swap_4_a_2),
    .B_2(separated_step_swap_4_b_2));
  separated_step_swap separated_step_swap_5 (
    .a(separated_step_swap_4_b_2), .b(separated_step_swap_3_a_2), .A_2(separated_step_swap_5_a_2), .B_2(_3));
  separated_step_swap separated_step_swap_6 (
    .a(separated_step_swap_4_a_2), .b(separated_step_swap_5_a_2), .A_2(_1), .B_2(_2));
endmodule

module _1bit_swap (
  input  I1,
  input  I2,
  input  S,
  output O1,
  output O2
);

  wire and_1_out, and_2_out, and_3_out, and_4_out, not_1_out;

  not not_1 (not_1_out, S);
  and and_1 (and_1_out, I1, not_1_out);
  and and_2 (and_2_out, I1, S);
  and and_3 (and_3_out, I2, S);
  and and_4 (and_4_out, I2, not_1_out);
  or or_1 (O1, and_1_out, and_3_out);
  or or_2 (O2, and_2_out, and_4_out);
endmodule

module _4bit_swap (
  input  [3:0] I1,
  input  [3:0] I2,
  input  S,
  output [3:0] O1,
  output [3:0] O2
);

  _1bit_swap u_1bit_swap_1 (.I1(I1[0]), .I2(I2[0]), .S(S), .O1(O1[0]), .O2(O2[0]));
  _1bit_swap u_1bit_swap_2 (.I1(I1[1]), .I2(I2[1]), .S(S), .O1(O1[1]), .O2(O2[1]));
  _1bit_swap u_1bit_swap_3 (.I1(I1[2]), .I2(I2[2]), .S(S), .O1(O1[2]), .O2(O2[2]));
  _1bit_swap u_1bit_swap_4 (.I1(I1[3]), .I2(I2[3]), .S(S), .O1(O1[3]), .O2(O2[3]));
endmodule

module separated_step_swap (
  input  [3:0] a,
  input  [3:0] b,
  output [3:0] A_2,
  output [3:0] B_2
);

  wire comparator_1_gt;

  Comparator #(.width(4), .mode("unsigned")) comparator_1 (.a(a), .b(b), .gt(comparator_1_gt));  // open: eq, lt
  _4bit_swap u_4bit_swap_1 (.I1(a), .I2(b), .S(comparator_1_gt), .O1(A_2), .O2(B_2));
endmodule
