// Logisim project test.circ as structural Verilog: 1 circuit, main circuit main
module main (
  input  [5:0] in_1,
  input  in_2,
  input  in_3,
  input  [3:0] in_4,
  output [2:0] out_5,
  output out_6,
  output [3:0] out_7
);

  wire and_1_out, and_2_out, not_1_out, not_2_out;
  wire [3:0] bit_extender_1_out, negator_1_out, shifter_1_out;

  not not_1 (not_1_out, in_2);
  not not_2 (not_2_out, in_3);
  and and_1 (and_1_out, in_2, not_2_out);
  assign bit_extender_1_out = {{2{1'b1}}, 2'b10};  // Bit_Extender bit_extender_1
  Shifter #(.width(4), .shift("ar")) shifter_1 (.in(in_4), .\dist (2'b10), .out(shifter_1_out));
  assign out_5 = ~(in_1[2:0] ^ in_1[5:3]);  // XNOR_Gate xnor_1, 3 bits wide
  and and_2 (and_2_out, not_1_out, in_3);
  // Probe on bit_extender_1_out
  // Probe on shifter_1_out
  // Probe on out_5
  or or_1 (out_6, and_2_out, and_1_out);
  // Probe on negator_1_out
  Negator #(.width(4)) negator_1 (.in(bit_extender_1_out), .out(negator_1_out));
  // Probe on out_7
  assign out_7 = negator_1_out ^ shifter_1_out;  // Odd_Parity odd_parity_1, 4 bits wide
endmodule
